// Logisim project adders.circ as structural Verilog: 1 circuit, main circuit main
module main (
  input  A,
  input  B,
  input  in_3,
  input  in_4,
  input  in_5,
  output SUM,
  output CARRY,
  output out_8,
  output out_9
);

  wire and_1_out, and_3_out, xor_1_out;

  xor xor_1 (xor_1_out, in_3, in_4);
  and and_1 (and_1_out, in_3, in_4);
  xor xor_2 (SUM, A, B);
  and and_2 (CARRY, A, B);
  xor xor_3 (out_8, xor_1_out, in_5);
  and and_3 (and_3_out, xor_1_out, in_5);
  or or_1 (out_9, and_3_out, and_1_out);
endmodule
